# Fritzing sketch inputs-force-sensor (saved by Fritzing 0.9.3b)

parts:
  J1 = Basic Force Sensing Resistor (FSR) [package=THT]
  R1 = Resistor [tolerance=±5% resistance=10k package="1206 [SMD]"]
  Part2 = Adafruit Flora [part_number="Adafruit #659"]

nets:
  N1: J1.pin_0, Part2.VBAT
  N2: J1.pin_1, R1.Pin_0, Part2.IO10
  N3: R1.Pin_1, Part2.GND

custom parts:
  Adafruit Flora: FLORA is Adafruit's fully-featured wearable electronics platform. It's a round, sewable, Arduino-compatible microcontroller designed to empower amazing wearables projects. The FLORA is small (1.75" diameter, weighing 4.4 grams). The FLORA has built-in USB support. Built in USB means you plug it in to program it, it just shows up - all you need is a Micro-B USB cable, no additional purchases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
