# Fritzing sketch inputs-tilt-ball-switch (saved by Fritzing 0.9.3b)

parts:
  Part3 = Adafruit Flora [part_number="Adafruit #659"]
  S2 = Tilt Switch [package=THT]

nets:
  N1: Part3.GND, S2.Pin_2
  N2: Part3.IO12, S2.Pin_1

custom parts:
  Adafruit Flora: FLORA is Adafruit's fully-featured wearable electronics platform. It's a round, sewable, Arduino-compatible microcontroller designed to empower amazing wearables projects. The FLORA is small (1.75" diameter, weighing 4.4 grams). The FLORA has built-in USB support. Built in USB means you plug it in to program it, it just shows up - all you need is a Micro-B USB cable, no additional purchases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
