# Fritzing sketch inputs-uv-light-sensor (saved by Fritzing 0.9.3b)

parts:
  Part1 = Adafruit Flora [part_number="Adafruit #659"]
  Part3 = Flora SI1145 UV Sensor

nets:
  +3V3: Part1.+3V3, Part3.3.3V
  GND: Part1.GND, Part3.GND
  N1: Part1.IO2/SDA, Part3.SCL
  N2: Part1.IO3/SCL, Part3.SDA

custom parts:
  Adafruit Flora: FLORA is Adafruit's fully-featured wearable electronics platform. It's a round, sewable, Arduino-compatible microcontroller designed to empower amazing wearables projects. The FLORA is small (1.75" diameter, weighing 4.4 grams). The FLORA has built-in USB support. Built in USB means you plug it in to program it, it just shows up - all you need is a Micro-B USB cable, no additional purchases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
  Flora SI1145 UV Sensor: Your wearable can now keep you from getting sunburnt, with the Flora digital UV index sensor. We took our popular SI1145 UV index sensor and cut out everything you don't need for using with a Flora. It's small, round, and connects to the I2C bus pads. Flora can even use our library code to get calibrated light level and UV index data from the sensor. Please note: this sensor can be used by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
