# Fritzing sketch lights-neopixel-24-ring (saved by Fritzing 0.9.3b)

parts:
  Part1 = 24 NeoPixel Ring [part_number=1586]
  Part2 = Adafruit Flora [part_number="Adafruit #659"]

nets:
  N1: Part1.IN, Part2.IO10
  GND: Part1.GND, Part2.GND
  N2: Part1.VDD, Part2.VBAT

custom parts:
  24 NeoPixel Ring: 24 ultra bright smart LED NeoPixels are arranged in a circle with 2.6" (66mm) outer diameter. The rings are 'chainable' - connect the output pin of one to the input pin of another. Use only one microcontroller pin to control as many as you can chain together! Each LED is addressable as the driver chip is inside the LED. Each one has ~18mA constant current drive so the color will be very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
  Adafruit Flora: FLORA is Adafruit's fully-featured wearable electronics platform. It's a round, sewable, Arduino-compatible microcontroller designed to empower amazing wearables projects. The FLORA is small (1.75" diameter, weighing 4.4 grams). The FLORA has built-in USB support. Built in USB means you plug it in to program it, it just shows up - all you need is a Micro-B USB cable, no additional purchases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
