# Fritzing sketch lights-neopixel-60-strip (saved by Fritzing 0.9.3b)

parts:
  Part2 = Adafruit Flora [part_number="Adafruit #659"]
  NEOPIXEL1 = Neopixel Strip -- White (60/m) [part_number=1138]

nets:
  GND: Part2.GND, NEOPIXEL1.GND
  N1: Part2.IO10, NEOPIXEL1.DI
  N2: Part2.VBAT, NEOPIXEL1.+5V

custom parts:
  Adafruit Flora: FLORA is Adafruit's fully-featured wearable electronics platform. It's a round, sewable, Arduino-compatible microcontroller designed to empower amazing wearables projects. The FLORA is small (1.75" diameter, weighing 4.4 grams). The FLORA has built-in USB support. Built in USB means you plug it in to program it, it just shows up - all you need is a Micro-B USB cable, no additional purchases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
  Neopixel Strip -- White (60/m): Neopixel Strip, White, 60 pixels per meter.
