# Fritzing sketch lights-neopixel-7-jewel (saved by Fritzing 0.9.3b)

parts:
  Part2 = Adafruit Flora [part_number="Adafruit #659"]
  Part4 = NeoPixel Jewel [part_number=2226]

nets:
  GND: Part2.GND, Part4.GND
  N1: Part2.IO10, Part4.IN
  N2: Part2.VBAT, Part4.VDD

custom parts:
  Adafruit Flora: FLORA is Adafruit's fully-featured wearable electronics platform. It's a round, sewable, Arduino-compatible microcontroller designed to empower amazing wearables projects. The FLORA is small (1.75" diameter, weighing 4.4 grams). The FLORA has built-in USB support. Built in USB means you plug it in to program it, it just shows up - all you need is a Micro-B USB cable, no additional purchases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
  NeoPixel Jewel: We fit seven of our tiny 5050 (5mm x 5mm) smart RGB LEDs onto a beautiful, round PCB with mounting holes and a chainable design to create what we think is our most elegant (and evening-wear appropriate) NeoPixel board yet. Use only one microcontroller pin to control as many as you can chain together! Each LED is addressable as the driver chip is inside the LED. Each one has ~18mA constant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
