# Fritzing sketch lights-neopixel (saved by Fritzing 0.9.3b)

parts:
  Part2 = Adafruit Flora [part_number="Adafruit #659"]
  LED1 = prefix0000

nets:
  N1: Part2.GND, LED1.connector3
  N2: Part2.IO10, LED1.connector2
  N3: Part2.VBAT, LED1.connector1

custom parts:
  Adafruit Flora: FLORA is Adafruit's fully-featured wearable electronics platform. It's a round, sewable, Arduino-compatible microcontroller designed to empower amazing wearables projects. The FLORA is small (1.75" diameter, weighing 4.4 grams). The FLORA has built-in USB support. Built in USB means you plug it in to program it, it just shows up - all you need is a Micro-B USB cable, no additional purchases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
