# Fritzing sketch lights-sequins (saved by Fritzing 0.9.3b)

parts:
  Part2 = Adafruit Flora [part_number="Adafruit #659"]
  Part3 = LED Sequin - Ruby Red [part_number=1755]

nets:
  N1: Part2.GND, Part3.-
  N2: Part2.IO10, Part3.+

custom parts:
  Adafruit Flora: FLORA is Adafruit's fully-featured wearable electronics platform. It's a round, sewable, Arduino-compatible microcontroller designed to empower amazing wearables projects. The FLORA is small (1.75" diameter, weighing 4.4 grams). The FLORA has built-in USB support. Built in USB means you plug it in to program it, it just shows up - all you need is a Micro-B USB cable, no additional purchases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
  LED Sequin - Ruby Red: Sew a little sparkle into your wearable project with an Adafruit LED Sequin. Simply connect 3 to 6VDC to the + pin and ground to the - pin, and the LED on the board will light up. You can make the LEDs fade and twinkle by using PWM.
